// Logisim project Mikroprozessor_A_8_v0.1.circ as structural Verilog: 2 circuits, main circuit main
module main (
);

  wire adder_1_cout, Ain, ALo, and_1_out, and_2_out, and_3_out, and_5_out, and_6_out, Bin, button_1_out, Cin,
       CLK, clock_1_out, Cot, Fin, HLT, JMC, JMP, JMZ, ldJ, ldS, Mot, nor_1_out, not_1_out, not_2_out, Oin,
       Oot, or_1_out, RAi, Rin, Rot, s_r_ff_1_q, seS, subtractor_1_bout;
  wire [1:0] counter_1_q;
  wire [3:0] bt_13_out_3, register_7_q, register_7_q_2, undriven_2;
  wire [7:0] adder_1_out, bt_3_out_3, bt_5_out_3, bt_7_out_3, ram_1_dout, register_1_q, register_2_q,
       register_3_q, register_4_q, register_5_q, register_6_q, register_8_q, register_9_q, rom_1_data,
       subtractor_1_out;
  wire [7:7] bt_11_out_3;
  wire [8:0] counter_2_q_2, undriven;
  wire [8:1] counter_2_q;
  wire [19:0] rom_2_data;

  not not_1 (not_1_out, counter_1_q[1]);
  and and_1 (and_1_out, CLK, not_1_out);
  Button button_1 (.out(button_1_out));
  and and_2 (and_2_out, counter_1_q[1], CLK);
  Counter #(.max('h3), .width(2)) counter_1 (.clk(and_1_out), .Q(counter_1_q));  // open: clr, load, up, count, D, carry
  Counter #(.max('h1ff), .width(9)) counter_2 (
    .clr(button_1_out), .clk(and_2_out), .D(undriven), .Q({counter_2_q, counter_2_q_2[0]}));  // open: load, up, count, carry
  Register register_1 (.D(bt_5_out_3), .en(ldJ), .clk(CLK), .Q(register_1_q));  // open: clr
  Register register_2 (.D(bt_5_out_3), .en(Ain), .clk(CLK), .Q(register_2_q));  // open: clr
  Register register_3 (.D(bt_5_out_3), .en(Bin), .clk(CLK), .Q(register_3_q));  // open: clr
  BT bt_1 (.in_1(register_1_q), .in_2(or_1_out), .out_3(undriven[8:1]));
  and and_3 (and_3_out, adder_1_cout, register_5_q[0]);
  and and_4 (and_3_out, subtractor_1_bout, register_5_q[1]);
  Register register_4 (.D(counter_2_q), .en(ldS), .clk(CLK), .Q(register_4_q));  // open: clr
  or or_1 (or_1_out, and_6_out, JMP, and_5_out);
  and and_5 (and_5_out, and_3_out, JMC);
  Register register_5 (.D(bt_5_out_3), .en(Fin), .clk(CLK), .Q(register_5_q));  // open: clr
  Adder adder_1 (.a(register_2_q), .b(register_3_q), .out(adder_1_out), .cout(adder_1_cout));  // open: cin
  Subtractor subtractor_1 (
    .a(register_2_q), .b(register_3_q), .out(subtractor_1_out), .bout(subtractor_1_bout));  // open: bin
  BT bt_2 (.in_1(register_4_q), .in_2(seS), .out_3(undriven[8:1]));
  BT bt_3 (.in_1(adder_1_out), .in_2(register_5_q[0]), .out_3(bt_3_out_3));
  BT bt_4 (.in_1(subtractor_1_out), .in_2(register_5_q[1]), .out_3(bt_3_out_3));
  and and_6 (and_6_out, JMZ, nor_1_out);
  nor nor_1 (nor_1_out, register_6_q[7], register_6_q[6], register_6_q[5], register_6_q[4], register_6_q[3], register_6_q[2], register_6_q[1], register_6_q[0]);
  Register register_6 (.D(bt_3_out_3), .en(1'b1), .clk(CLK), .Q(register_6_q));  // open: clr
  ROM #(.dataWidth(16)) rom_1 (.addr(counter_2_q), .data({counter_2_q_2[8:1], rom_1_data}));
  BT bt_5 (.in_1(register_6_q), .in_2(ALo), .out_3(bt_5_out_3));
  Hex_Digit_Display hex_digit_display_1 (.value(register_7_q_2));  // open: dp
  Register register_7 (.D(bt_5_out_3), .en(Oin), .clk(CLK), .Q({register_7_q_2, register_7_q}));  // open: clr
  Hex_Digit_Display hex_digit_display_2 (.value(register_7_q));  // open: dp
  BT bt_6 (.in_1({register_7_q_2, register_7_q}), .in_2(Oot), .out_3(bt_5_out_3));
  Register register_8 (.D(bt_5_out_3), .en(RAi), .clk(CLK), .Q(register_8_q));  // open: clr
  RAM ram_1 (.addr(register_8_q), .we(Rin), .oe(1'b1), .clk(CLK), .din(bt_5_out_3), .dout(ram_1_dout));
  BT bt_7 (.in_1(rom_1_data), .in_2(Mot), .out_3(bt_7_out_3));
  not not_2 (not_2_out, Mot);
  Clock clock_1 (.out(clock_1_out));
  S_R_Flip_Flop s_r_ff_1 (.S(HLT), .clk(CLK), .Q(s_r_ff_1_q));  // open: R, reset, Qn, preset
  // Buffer buffer_1 is placed but not wired
  Register #(.trigger("high")) register_9 (.D(bt_7_out_3), .en(Cin), .clk(CLK), .Q(register_9_q));  // open: clr
  BT bt_8 (.in_1(bt_5_out_3), .in_2(not_2_out), .out_3(bt_7_out_3));
  xor xor_1 (CLK, clock_1_out, s_r_ff_1_q);
  ROM #(.addrWidth(9), .dataWidth(20)) rom_2 (.addr(counter_2_q_2), .data(rom_2_data));
  BT bt_9 (.in_1(register_9_q), .in_2(Cot), .out_3(bt_5_out_3));
  BT bt_10 (.in_1(ram_1_dout), .in_2(Rot), .out_3(bt_5_out_3));
  BT bt_11 (.in_1(rom_2_data[19:12]), .in_2(CLK), .out_3({bt_11_out_3[7], Oot, Oin, JMZ, JMC, JMP, ldJ, seS}));
  // Probe on rom_2_data
  BT bt_12 (.in_1(rom_2_data[11:4]), .in_2(CLK), .out_3({ldS, ALo, Fin, Rot, Rin, RAi, Mot, Cot}));
  BT bt_13 (.in_1({rom_2_data[3:0], undriven_2}), .in_2(CLK), .out_3({Cin, Bin, Ain, HLT, bt_13_out_3}));

  // Notes on the sheet:
  //   contents of rom_1 (hex, n*v repeats v):
  //   5ff 400 d00 c00
  //   contents of rom_2 (hex, n*v repeats v):
  //   60 102 60 104 60 108 60 90 28 0 28 0 60 300 10000 8000 4000 0 1 0 60 20100 60 40080
endmodule

module BT (
  input  [7:0] in_1,
  input  in_2,
  output [7:0] out_3
);

  Transistor #(.\type ("n"), .width(8)) transistor_1 (.in(in_1), .out(out_3), .gate(in_2));
endmodule
